// Logisim project projet.circ as structural Verilog
module ADD_SUB (
  input  [31:0] in1,
  input  [31:0] in2,
  input  sub,
  output [31:0] out_4,
  output Overflow,
  output Carry
);

  wire adder_2_cout, xor_1_out;
  wire [31:0] adder_1_out, multiplexer_1_out, not_1_out;

  assign not_1_out = ~in2;  // NOT_Gate not_1, 32 bits wide
  Adder #(.width(32)) adder_1 (.a(not_1_out), .b(32'h1), .out(adder_1_out));  // open: cin, cout
  Multiplexer #(.width(32), .enable("false")) multiplexer_1 (
    .in0(in2), .in1(adder_1_out), .out(multiplexer_1_out), .sel(sub));
  Adder #(.width(31)) adder_2 (
    .a(in1[30:0]), .b(multiplexer_1_out[30:0]), .out(out_4[30:0]), .cout(adder_2_cout));  // open: cin
  Adder #(.width(1)) adder_3 (
    .a(in1[31]), .b(multiplexer_1_out[31]), .out(out_4[31]), .cin(adder_2_cout), .cout(Carry));
  xor xor_1 (xor_1_out, adder_2_cout, Carry);
  Multiplexer #(.enable("false")) multiplexer_2 (.in0(1'b0), .in1(xor_1_out), .out(Overflow), .sel(sub));

  // Notes on the sheet:
  //   adder3
  //   adder1
  //   adder2
endmodule

module ALU (
  input  sub,
  input  [31:0] s1,
  input  [31:0] s2,
  input  [2:0] aluop,
  output C,
  output V,
  output [31:0] out,
  output Z,
  output N
);

  wire [31:0] add_sub_1_out_4, and_1_out, multiplier_1_out, or_1_out, xor_1_out;

  ADD_SUB add_sub_1 (.in1(s1), .in2(s2), .sub(sub), .out_4(add_sub_1_out_4), .Carry(C), .Overflow(V));
  assign and_1_out = s1 & s2;  // AND_Gate and_1, 32 bits wide
  assign or_1_out = s1 | s2;  // OR_Gate or_1, 32 bits wide
  assign xor_1_out = s1 ^ s2;  // XOR_Gate xor_1, 32 bits wide
  Multiplier #(.width(32)) multiplier_1 (.a(s1), .b(s2), .out(multiplier_1_out));  // open: cin, cout
  Multiplexer #(.select(3), .width(32), .enable("false")) multiplexer_1 (
    .in0(add_sub_1_out_4), .in1(and_1_out), .in2(or_1_out), .in3(xor_1_out), .in4(multiplier_1_out),
    .out(out), .sel(aluop));  // open: in5, in6, in7
  Comparator #(.width(32)) comparator_1 (.a(out), .b({32{1'b0}}), .eq(Z), .lt(N));  // open: gt
endmodule

module FLAGS (
  input  Z,
  input  C,
  input  N,
  input  V,
  input  [3:0] cond,
  output out
);

  wire and_1_out, and_2_out, comparator_1_eq, comparator_1_gt, comparator_1_lt, not_1_out, not_2_out,
       not_3_out, not_4_out, or_1_out, or_2_out, or_3_out;

  not not_1 (not_1_out, Z);
  not not_2 (not_2_out, C);
  not not_3 (not_3_out, N);
  not not_4 (not_4_out, V);
  and and_1 (and_1_out, not_1_out, C);
  Multiplexer #(.select(4), .enable("false")) multiplexer_1 (
    .in0(Z), .in1(not_1_out), .in2(C), .in3(not_2_out), .in4(N), .in5(not_3_out), .in6(V), .in7(not_4_out),
    .in8(and_1_out), .in9(or_1_out), .in10(comparator_1_eq), .in11(or_2_out), .in12(and_2_out),
    .in13(or_3_out), .in14(1'b1), .out(out), .sel(cond));  // open: in15
  or or_1 (or_1_out, not_2_out, Z);
  Comparator #(.width(1), .mode("unsigned")) comparator_1 (
    .a(N), .b(V), .gt(comparator_1_gt), .eq(comparator_1_eq), .lt(comparator_1_lt));
  or or_2 (or_2_out, comparator_1_lt, comparator_1_gt);
  or or_3 (or_3_out, or_2_out, Z);
  and and_2 (and_2_out, comparator_1_eq, not_1_out);
endmodule

module REG_PC (
  input  [31:0] rd,
  input  we,
  input  [3:0] m,
  input  [3:0] n,
  input  [3:0] d,
  input  reset,
  input  CLK,
  output [31:0] rn,
  output [31:0] rm
);

  wire demultiplexer_1_out0, demultiplexer_1_out1, demultiplexer_1_out2, demultiplexer_1_out3,
       demultiplexer_1_out4, demultiplexer_1_out5, demultiplexer_1_out6, demultiplexer_1_out7,
       demultiplexer_1_out8, demultiplexer_1_out9, demultiplexer_1_out10, demultiplexer_1_out11,
       demultiplexer_1_out12, demultiplexer_1_out13, demultiplexer_1_out14, undriven;
  wire [31:0] r0_q, r1_q, r2_q, r3_q, r4_q, r5_q, r6_q, r7_q, r9_q, r10_q, r11_q, r12_q, r13_q;

  Demultiplexer #(.select(4), .enable("false")) demultiplexer_1 (
    .out0(demultiplexer_1_out0), .out1(demultiplexer_1_out1), .out2(demultiplexer_1_out2),
    .out3(demultiplexer_1_out3), .out4(demultiplexer_1_out4), .out5(demultiplexer_1_out5),
    .out6(demultiplexer_1_out6), .out7(demultiplexer_1_out7), .out8(demultiplexer_1_out8),
    .out9(demultiplexer_1_out9), .out10(demultiplexer_1_out10), .out11(demultiplexer_1_out11),
    .out12(demultiplexer_1_out12), .out13(demultiplexer_1_out13), .out14(demultiplexer_1_out14),
    .in(undriven), .sel(d));  // open: out15
  Register #(.width(32)) r0 (.D(rd), .en(demultiplexer_1_out0), .Q(r0_q), .clk(CLK), .clr(reset));
  Register #(.width(32)) r1 (.D(rd), .en(demultiplexer_1_out1), .Q(r1_q), .clk(CLK), .clr(reset));
  Register #(.width(32)) r2 (.D(rd), .en(demultiplexer_1_out2), .Q(r2_q), .clk(CLK), .clr(reset));
  Register #(.width(32)) r3 (.D(rd), .en(demultiplexer_1_out3), .Q(r3_q), .clk(CLK), .clr(reset));
  Register #(.width(32)) r4 (.D(rd), .en(demultiplexer_1_out4), .Q(r4_q), .clk(CLK), .clr(reset));
  Register #(.width(32)) r5 (.D(rd), .en(demultiplexer_1_out5), .Q(r5_q), .clk(CLK), .clr(reset));
  Register #(.width(32)) r6 (.D(rd), .en(demultiplexer_1_out6), .Q(r6_q), .clk(CLK), .clr(reset));
  Register #(.width(32)) r7 (.D(rd), .en(demultiplexer_1_out7), .Q(r7_q), .clk(CLK), .clr(reset));
  Register #(.width(32)) r8 (.D(rd), .en(demultiplexer_1_out8), .Q(r7_q), .clk(CLK), .clr(reset));
  Register #(.width(32)) r9 (.D(rd), .en(demultiplexer_1_out9), .Q(r9_q), .clk(CLK), .clr(reset));
  Register #(.width(32)) r10 (.D(rd), .en(demultiplexer_1_out10), .Q(r10_q), .clk(CLK), .clr(reset));
  Register #(.width(32)) r11 (.D(rd), .en(demultiplexer_1_out11), .Q(r11_q), .clk(CLK), .clr(reset));
  Register #(.width(32)) r12 (.D(rd), .en(demultiplexer_1_out12), .Q(r12_q), .clk(CLK), .clr(reset));
  Register #(.width(32)) r13 (.D(rd), .en(demultiplexer_1_out13), .Q(r13_q), .clk(CLK), .clr(reset));
  Register #(.width(32)) r14 (.en(demultiplexer_1_out14), .clk(CLK));  // open: D, Q, clr
  Register #(.width(32)) r15 (.en(1'b1), .clk(CLK), .clr(reset));  // open: D, Q
  Multiplexer #(.select(4), .width(32), .enable("false")) multiplexer_1 (
    .in0(r0_q), .in1(r1_q), .in2(r2_q), .in3(r3_q), .in4(r4_q), .in5(r5_q), .in6(r6_q), .in7(r7_q),
    .in8(r7_q), .in9(r9_q), .in10(r10_q), .in11(r11_q), .in12(r12_q), .in13(r13_q), .out(rn), .sel(n));  // open: in14, in15
  Multiplexer #(.select(4), .width(32), .enable("false")) multiplexer_2 (
    .in0(r0_q), .in1(r1_q), .in2(r2_q), .in3(r3_q), .in4(r4_q), .in5(r5_q), .in6(r6_q), .in7(r7_q),
    .in8(r7_q), .in9(r9_q), .in10(r10_q), .in11(r11_q), .in12(r12_q), .in13(r13_q), .out(rm), .sel(m));  // open: in14, in15
endmodule
